// Digital circuit Lab00a.dig as structural Verilog
module Lab00a (
);

  wire switch1_b;

  Switch switch1 (.A(1'b1), .B(switch1_b));
  // PolarityAwareLED led1: pin names not known; wires that end beside it: switch1_b, 1'b0
endmodule
