// Digital circuit Lab00b.dig as structural Verilog
module Lab00b (
);

  Switch #(.switchActsAsInput("true")) switch1 ();  // open: A, B
  Switch #(.switchActsAsInput("true")) switch2 ();  // open: A, B
  // PolarityAwareLED led1: pin names not known; wires that end beside it: 1'b1, 1'b0
endmodule
