// Digital circuit and.dig as structural Verilog
module \and  (
);

  wire switch_0_b, switch_1_b;

  Switch #(.switchActsAsInput("true")) switch_0 (.A(1'b1), .B(switch_0_b));
  Switch #(.switchActsAsInput("true")) switch_1 (.A(switch_0_b), .B(switch_1_b));
  // PolarityAwareLED LED: pin names not known; wires that end beside it: switch_1_b, 1'b0
endmodule

/* Test case:
switch_0 switch_1 LED
0 0 Z
0 1 Z
1 0 Z
1 1 1
*/
