// Digital circuit example.dig as structural Verilog
module example (
);

  wire switch_b;

  Switch #(.switchActsAsInput("true")) switch (.A(1'b1), .B(switch_b));
  // PolarityAwareLED LED: pin names not known; wires that end beside it: switch_b, 1'b0
endmodule

/* Test case:
switch LED
0 Z
1 1
*/
