// Digital circuit splitter.dig as structural Verilog
module splitter (
  input  [9:0] in,
  output out
);

  and and_1 (out, in[0], in[9]);
endmodule

/* Test case:
in out

# positive even
0b0101011000 0
0b0110000100 0

# positive odd
0b0110010111 0
0b0111111111 0

# negative even
0b1001000110 0
0b1010001110 0

# negative odd
0b1011101101 1
0b1110011001 1
*/
